// Logisim project alu_architecture.circ as structural Verilog: 6 circuits, main circuit ALU_TOP
module ADDER_SUBTRACTOR (
  input  [7:0] op1,
  input  [7:0] op2,
  input  sub_mode,
  output [7:0] result,
  output c_out
);

  // Bit_Extender #(.in_width(1), .out_width(8), .\type ("zero")) bit_extender_1: pin names not known; wires that end beside it: op2
  // XOR_Gate xor_1 has open pins: out=op2
  Adder #(.width(8)) adder_1 (.a(op1), .b(op2));  // open: out, cin, cout
  // Pins of 1 and 8 bits meet at op2

  assign sub_mode = op2[0];
endmodule

module BOOTH_MULTIPLIER (
  input  [7:0] A,
  input  [7:0] B,
  input  start,
  output [7:0] product_lo,
  output [7:0] product_hi,
  output done
);

  Multiplier #(.width(8)) multiplier_1 (.a(A), .b(B));  // open: out, cin, cout

  assign done = start;
endmodule

module RADIX2_DIVIDER (
  input  [7:0] A,
  input  [7:0] B,
  input  start,
  output [7:0] quotient,
  output [7:0] remainder,
  output done
);

  Divider #(.width(8)) divider_1 (.a(A), .b(B));  // open: out, upper, rem

  assign done = start;
endmodule

module CONTROL_UNIT (
  input  clk,
  input  rst,
  input  start,
  input  exec_done,
  input  exec_busy,
  output load_en,
  output exec_start,
  output done
);

  Register #(.width(2)) STATE ();  // open: D, en, clk, Q, clr

  assign done = exec_done;
  assign exec_start = start;
  assign load_en = exec_busy;
endmodule

module REGISTER_8BIT (
  input  [7:0] data_in,
  input  load_en,
  input  clk,
  input  rst,
  output [7:0] data_out
);

  // Register #(.width(8)) REG: pin names not known; wires that end beside it: load_en, clk, rst
endmodule

module ALU_TOP (
  input  clk,
  input  rst,
  input  start,
  input  [1:0] opcode,
  input  [7:0] A_raw,
  input  [7:0] B_raw,
  output carry_out,
  output overflow,
  output [15:0] result,
  output done
);

  wire adder_subtractor_1_p3, multiplexer_1_p1, multiplexer_1_p2;
  wire [7:0] adder_subtractor_1_p2;

  // CONTROL_UNIT control_unit_1: pin names not known; wires that end beside it: rst, start
  // REGISTER_8BIT register_8bit_1: pin names not known; wires that end beside it: A_raw, B_raw
  // REGISTER_8BIT register_8bit_2: pin names not known; wires that end beside it: B_raw
  // ADDER_SUBTRACTOR adder_subtractor_1: pin names not known; wires that end beside it: done, adder_subtractor_1_p2, adder_subtractor_1_p3
  BOOTH_MULTIPLIER booth_multiplier_1 (.product_lo(adder_subtractor_1_p2));  // open: A, B, start, product_hi, done
  // RADIX2_DIVIDER radix2_divider_1: pin names not known; wires that end beside it: adder_subtractor_1_p3
  // Multiplexer #(.enable("false"), .select(2), .width(16)) multiplexer_1: pin names not known; wires that end beside it: multiplexer_1_p1, multiplexer_1_p2

  // Notes on the sheet:
  //   Control Unit (FSM)
  //   Operand Registers
  //   Structural 8-bit ALU (Top-Level)
  //   ADD/SUB
  //   MULTIPLIER
  //   DIVIDER
  //   Arithmetic Engines
  //   Result MUX
endmodule
